// Logisim project trafficlightcontrollerfsm.circ as structural Verilog: 5 circuits, main circuit main
module main (
  input  C
);

  wire clock_1_out, counter_1_carry, counter_2_carry, D0_d0, D1_d1, decoder_1_out0, decoder_1_out1,
       decoder_1_out2, decoder_1_out3, or_1_out, or_2_out;
  wire [1:0] d_ff_1_q;

  Clock clock_1 (.out(clock_1_out));
  D0 D0 (.Q1(d_ff_1_q[1]), .Q0(d_ff_1_q[0]), .Tl(counter_2_carry), .C(C), .Ts(counter_1_carry), .D0(D0_d0));
  D_Flip_Flop d_ff_1 (.clk(clock_1_out), .D(D0_d0), .Q(d_ff_1_q[0]));  // open: Qn, preset, en, reset
  Counter #(.width(3), .max('h5)) counter_1 (
    .count(1'b1), .carry(counter_1_carry), .clk(clock_1_out));  // open: load, D, Q, clr
  D1 D1 (.Q1(d_ff_1_q[1]), .Q0(d_ff_1_q[0]), .Tl(counter_2_carry), .C(C), .Ts(counter_1_carry), .D1(D1_d1));
  Counter #(.width(3), .max('h7)) counter_2 (
    .count(1'b1), .carry(counter_2_carry), .clk(clock_1_out));  // open: load, D, Q, clr
  D_Flip_Flop d_ff_2 (.clk(clock_1_out), .D(D1_d1), .Q(d_ff_1_q[1]));  // open: Qn, preset, en, reset
  Decoder #(.select(2)) decoder_1 (
    .out0(decoder_1_out0), .out1(decoder_1_out1), .out2(decoder_1_out2), .out3(decoder_1_out3), .sel(d_ff_1_q));  // open: en
  or or_1 (or_1_out, decoder_1_out3, decoder_1_out2);
  LED led_1 (.in(or_1_out));
  LED led_2 (.in(decoder_1_out1));
  LED led_3 (.in(decoder_1_out0));
  or or_2 (or_2_out, decoder_1_out0, decoder_1_out1);
  LED led_4 (.in(or_2_out));
  LED led_5 (.in(decoder_1_out3));
  LED led_6 (.in(decoder_1_out2));

  // Notes on the sheet:
  //   Highway Lights
  //   NITK Lights
endmodule

module D1 (
  input  Q1,
  input  Q0,
  input  Tl,
  input  C,
  input  Ts,
  output D1
);

  wire and_1_out, and_2_out, and_3_out, not_1_out, not_2_out, not_3_out;

  not not_1 (not_1_out, Q1);
  not not_2 (not_2_out, Q0);
  not not_3 (not_3_out, Ts);
  and and_1 (and_1_out, not_1_out, Q0, Ts);
  and and_2 (and_2_out, Q1, not_2_out);
  and and_3 (and_3_out, Q1, not_3_out);
  or or_1 (D1, and_1_out, and_2_out, and_3_out);
endmodule

module D0 (
  input  Q1,
  input  Q0,
  input  Tl,
  input  C,
  input  Ts,
  output D0
);

  wire and_1_out, and_2_out, and_3_out, not_1_out, not_2_out, not_3_out, not_4_out;

  not not_1 (not_1_out, Q0);
  not not_2 (not_2_out, Ts);
  not not_3 (not_3_out, Q0);
  not not_4 (not_4_out, C);
  and and_1 (and_1_out, not_1_out, Tl, C);
  and and_2 (and_2_out, Q0, not_2_out);
  and and_3 (and_3_out, Q1, not_3_out, not_4_out);
  or or_1 (D0, and_1_out, and_2_out, and_3_out);
endmodule

module ST (
  input  Q1,
  input  Q0,
  input  Tl,
  input  C,
  input  Ts,
  output ST
);

  wire and_1_out, and_2_out, and_3_out, not_1_out, not_2_out, not_3_out;

  not not_1 (not_1_out, Q0);
  not not_2 (not_2_out, Q0);
  not not_3 (not_3_out, C);
  and and_1 (and_1_out, not_1_out, Tl, C);
  and and_2 (and_2_out, Q0, Ts);
  and and_3 (and_3_out, Q1, not_2_out, not_3_out);
  or or_1 (ST, and_1_out, and_2_out, and_3_out);
endmodule

module random (
  input  [1:0] in_1
);

  wire decoder_1_out0, decoder_1_out1, decoder_1_out2, decoder_1_out3;

  Decoder #(.select(2)) decoder_1 (
    .out0(decoder_1_out0), .out1(decoder_1_out1), .out2(decoder_1_out2), .out3(decoder_1_out3), .sel(in_1));  // open: en
endmodule
