// Logisim project digitalclock.circ as structural Verilog: 5 circuits, main circuit main
module main (
  input  Set_Time_Manually
);

  wire button_1_out, button_2_out, button_3_out, clock_3_out, n4bitto7segment_1_a, n4bitto7segment_1_b,
       n4bitto7segment_1_c, n4bitto7segment_1_d, n4bitto7segment_1_e, n4bitto7segment_1_f,
       n4bitto7segment_1_g, n4bitto7segment_2_a, n4bitto7segment_2_b, n4bitto7segment_2_c,
       n4bitto7segment_2_d, n4bitto7segment_2_e, n4bitto7segment_2_f, n4bitto7segment_2_g,
       n4bitto7segment_3_a, n4bitto7segment_3_b, n4bitto7segment_3_c, n4bitto7segment_3_d,
       n4bitto7segment_3_e, n4bitto7segment_3_f, n4bitto7segment_3_g, n4bitto7segment_4_a,
       n4bitto7segment_4_b, n4bitto7segment_4_c, n4bitto7segment_4_d, n4bitto7segment_4_e,
       n4bitto7segment_4_f, n4bitto7segment_4_g, n4bitto7segment_5_a, n4bitto7segment_5_b,
       n4bitto7segment_5_c, n4bitto7segment_5_d, n4bitto7segment_5_e, n4bitto7segment_5_f,
       n4bitto7segment_5_g, n4bitto7segment_6_a, n4bitto7segment_6_b, n4bitto7segment_6_c,
       n4bitto7segment_6_d, n4bitto7segment_6_e, n4bitto7segment_6_f, n4bitto7segment_6_g,
       n4bitto7segment_7_a, n4bitto7segment_7_b, n4bitto7segment_7_c, n4bitto7segment_7_d,
       n4bitto7segment_7_e, n4bitto7segment_7_f, n4bitto7segment_7_g, n4bitto7segment_8_a,
       n4bitto7segment_8_b, n4bitto7segment_8_c, n4bitto7segment_8_d, n4bitto7segment_8_e,
       n4bitto7segment_8_f, n4bitto7segment_8_g, n4bitto7segment_9_a, n4bitto7segment_9_b,
       n4bitto7segment_9_c, n4bitto7segment_9_d, n4bitto7segment_9_e, n4bitto7segment_9_f,
       n4bitto7segment_9_g, n4bitto7segment_10_a, n4bitto7segment_10_b, n4bitto7segment_10_c,
       n4bitto7segment_10_d, n4bitto7segment_10_e, n4bitto7segment_10_f, n4bitto7segment_10_g,
       n4bitto7segment_11_a, n4bitto7segment_11_b, n4bitto7segment_11_c, n4bitto7segment_11_d,
       n4bitto7segment_11_e, n4bitto7segment_11_f, n4bitto7segment_11_g, n4bitto7segment_12_a,
       n4bitto7segment_12_b, n4bitto7segment_12_c, n4bitto7segment_12_d, n4bitto7segment_12_e,
       n4bitto7segment_12_f, n4bitto7segment_12_g, n6bittobcd_1_ha1, n6bittobcd_1_ha2, n6bittobcd_1_ha3,
       n6bittobcd_1_ha4, n6bittobcd_1_op1, n6bittobcd_1_op2, n6bittobcd_1_op3, n6bittobcd_1_op4,
       n6bittobcd_2_ha1, n6bittobcd_2_ha2, n6bittobcd_2_ha3, n6bittobcd_2_ha4, n6bittobcd_2_op1,
       n6bittobcd_2_op2, n6bittobcd_2_op3, n6bittobcd_2_op4, n6bittobcd_3_ha1, n6bittobcd_3_ha2,
       n6bittobcd_3_ha3, n6bittobcd_3_ha4, n6bittobcd_3_op1, n6bittobcd_3_op2, n6bittobcd_3_op3,
       n6bittobcd_3_op4, n6bittobcd_4_ha1, n6bittobcd_4_ha2, n6bittobcd_4_ha3, n6bittobcd_4_ha4,
       n6bittobcd_4_op1, n6bittobcd_4_op2, n6bittobcd_4_op3, n6bittobcd_4_op4, n6bittobcd_5_ha1,
       n6bittobcd_5_ha2, n6bittobcd_5_ha3, n6bittobcd_5_ha4, n6bittobcd_5_op1, n6bittobcd_5_op2,
       n6bittobcd_5_op3, n6bittobcd_5_op4, n6bittobcd_6_ha1, n6bittobcd_6_ha2, n6bittobcd_6_ha3,
       n6bittobcd_6_ha4, n6bittobcd_6_op1, n6bittobcd_6_op2, n6bittobcd_6_op3, n6bittobcd_6_op4, nor_1_out,
       nor_2_out, or_1_out, or_2_out, Reset_Button_out;
  wire [5:0] clock_1_out_5, clock_2_out_5, clock_4_out_5, clock_5_out_5, hourclock_1_out_5, hourclock_2_out_5;

  Button button_1 (.out(button_1_out));
  _4bitto7segment u_4bitto7segment_1 (
    .in_1(n6bittobcd_1_op1), .in_2(n6bittobcd_1_op2), .in_3(n6bittobcd_1_op3), .in_4(n6bittobcd_1_op4),
    .a(n4bitto7segment_1_a), .b(n4bitto7segment_1_b), .c(n4bitto7segment_1_c), .d(n4bitto7segment_1_d),
    .e(n4bitto7segment_1_e), .f(n4bitto7segment_1_f), .g(n4bitto7segment_1_g));
  _7_Segment_Display u_7_segment_display_1 (
    .g(n4bitto7segment_1_g), .f(n4bitto7segment_1_f), .a(n4bitto7segment_1_a), .b(n4bitto7segment_1_b),
    .e(n4bitto7segment_1_e), .d(n4bitto7segment_1_d), .c(n4bitto7segment_1_c));  // open: dp
  clock clock_1 (.Set_Time(1'b0), .Clock(button_1_out), .out_5(clock_1_out_5));  // open: Time_Input, Reset
  _6bittobcd u_6bittobcd_1 (
    .a(clock_1_out_5[5]), .b(clock_1_out_5[4]), .c(clock_1_out_5[3]), .d(clock_1_out_5[2]),
    .e(clock_1_out_5[1]), .f(clock_1_out_5[0]), .op1(n6bittobcd_1_op1), .op2(n6bittobcd_1_op2),
    .op3(n6bittobcd_1_op3), .op4(n6bittobcd_1_op4), .ha1(n6bittobcd_1_ha1), .ha2(n6bittobcd_1_ha2),
    .ha3(n6bittobcd_1_ha3), .ha4(n6bittobcd_1_ha4));
  _4bitto7segment u_4bitto7segment_2 (
    .in_1(n6bittobcd_1_ha1), .in_2(n6bittobcd_1_ha2), .in_3(n6bittobcd_1_ha3), .in_4(n6bittobcd_1_ha4),
    .a(n4bitto7segment_2_a), .b(n4bitto7segment_2_b), .c(n4bitto7segment_2_c), .d(n4bitto7segment_2_d),
    .e(n4bitto7segment_2_e), .f(n4bitto7segment_2_f), .g(n4bitto7segment_2_g));
  _7_Segment_Display u_7_segment_display_2 (
    .g(n4bitto7segment_2_g), .f(n4bitto7segment_2_f), .a(n4bitto7segment_2_a), .b(n4bitto7segment_2_b),
    .e(n4bitto7segment_2_e), .d(n4bitto7segment_2_d), .c(n4bitto7segment_2_c));  // open: dp
  _4bitto7segment u_4bitto7segment_3 (
    .in_1(n6bittobcd_2_op1), .in_2(n6bittobcd_2_op2), .in_3(n6bittobcd_2_op3), .in_4(n6bittobcd_2_op4),
    .a(n4bitto7segment_3_a), .b(n4bitto7segment_3_b), .c(n4bitto7segment_3_c), .d(n4bitto7segment_3_d),
    .e(n4bitto7segment_3_e), .f(n4bitto7segment_3_f), .g(n4bitto7segment_3_g));
  _7_Segment_Display u_7_segment_display_3 (
    .g(n4bitto7segment_3_g), .f(n4bitto7segment_3_f), .a(n4bitto7segment_3_a), .b(n4bitto7segment_3_b),
    .e(n4bitto7segment_3_e), .d(n4bitto7segment_3_d), .c(n4bitto7segment_3_c));  // open: dp
  Button button_2 (.out(button_2_out));
  clock clock_2 (.Set_Time(1'b0), .Clock(button_2_out), .out_5(clock_2_out_5));  // open: Time_Input, Reset
  _6bittobcd u_6bittobcd_2 (
    .a(clock_2_out_5[5]), .b(clock_2_out_5[4]), .c(clock_2_out_5[3]), .d(clock_2_out_5[2]),
    .e(clock_2_out_5[1]), .f(clock_2_out_5[0]), .op1(n6bittobcd_2_op1), .op2(n6bittobcd_2_op2),
    .op3(n6bittobcd_2_op3), .op4(n6bittobcd_2_op4), .ha1(n6bittobcd_2_ha1), .ha2(n6bittobcd_2_ha2),
    .ha3(n6bittobcd_2_ha3), .ha4(n6bittobcd_2_ha4));
  _4bitto7segment u_4bitto7segment_4 (
    .in_1(n6bittobcd_2_ha1), .in_2(n6bittobcd_2_ha2), .in_3(n6bittobcd_2_ha3), .in_4(n6bittobcd_2_ha4),
    .a(n4bitto7segment_4_a), .b(n4bitto7segment_4_b), .c(n4bitto7segment_4_c), .d(n4bitto7segment_4_d),
    .e(n4bitto7segment_4_e), .f(n4bitto7segment_4_f), .g(n4bitto7segment_4_g));
  _7_Segment_Display u_7_segment_display_4 (
    .g(n4bitto7segment_4_g), .f(n4bitto7segment_4_f), .a(n4bitto7segment_4_a), .b(n4bitto7segment_4_b),
    .e(n4bitto7segment_4_e), .d(n4bitto7segment_4_d), .c(n4bitto7segment_4_c));  // open: dp
  _4bitto7segment u_4bitto7segment_5 (
    .in_1(n6bittobcd_3_op1), .in_2(n6bittobcd_3_op2), .in_3(n6bittobcd_3_op3), .in_4(n6bittobcd_3_op4),
    .a(n4bitto7segment_5_a), .b(n4bitto7segment_5_b), .c(n4bitto7segment_5_c), .d(n4bitto7segment_5_d),
    .e(n4bitto7segment_5_e), .f(n4bitto7segment_5_f), .g(n4bitto7segment_5_g));
  _7_Segment_Display u_7_segment_display_5 (
    .g(n4bitto7segment_5_g), .f(n4bitto7segment_5_f), .a(n4bitto7segment_5_a), .b(n4bitto7segment_5_b),
    .e(n4bitto7segment_5_e), .d(n4bitto7segment_5_d), .c(n4bitto7segment_5_c));  // open: dp
  Button button_3 (.out(button_3_out));
  hourclock hourclock_1 (.Set_Time(1'b0), .Clock(button_3_out), .out_5(hourclock_1_out_5));  // open: Time_Input, Reset
  _6bittobcd u_6bittobcd_3 (
    .a(hourclock_1_out_5[5]), .b(hourclock_1_out_5[4]), .c(hourclock_1_out_5[3]), .d(hourclock_1_out_5[2]),
    .e(hourclock_1_out_5[1]), .f(hourclock_1_out_5[0]), .op1(n6bittobcd_3_op1), .op2(n6bittobcd_3_op2),
    .op3(n6bittobcd_3_op3), .op4(n6bittobcd_3_op4), .ha1(n6bittobcd_3_ha1), .ha2(n6bittobcd_3_ha2),
    .ha3(n6bittobcd_3_ha3), .ha4(n6bittobcd_3_ha4));
  _4bitto7segment u_4bitto7segment_6 (
    .in_1(n6bittobcd_3_ha1), .in_2(n6bittobcd_3_ha2), .in_3(n6bittobcd_3_ha3), .in_4(n6bittobcd_3_ha4),
    .a(n4bitto7segment_6_a), .b(n4bitto7segment_6_b), .c(n4bitto7segment_6_c), .d(n4bitto7segment_6_d),
    .e(n4bitto7segment_6_e), .f(n4bitto7segment_6_f), .g(n4bitto7segment_6_g));
  _7_Segment_Display u_7_segment_display_6 (
    .g(n4bitto7segment_6_g), .f(n4bitto7segment_6_f), .a(n4bitto7segment_6_a), .b(n4bitto7segment_6_b),
    .e(n4bitto7segment_6_e), .d(n4bitto7segment_6_d), .c(n4bitto7segment_6_c));  // open: dp
  Button Reset_Button (.out(Reset_Button_out));
  _7_Segment_Display u_7_segment_display_7 (
    .g(n4bitto7segment_7_g), .f(n4bitto7segment_7_f), .a(n4bitto7segment_7_a), .b(n4bitto7segment_7_b),
    .e(n4bitto7segment_7_e), .d(n4bitto7segment_7_d), .c(n4bitto7segment_7_c));  // open: dp
  Clock clock_3 (.out(clock_3_out));
  _4bitto7segment u_4bitto7segment_7 (
    .in_1(n6bittobcd_4_op1), .in_2(n6bittobcd_4_op2), .in_3(n6bittobcd_4_op3), .in_4(n6bittobcd_4_op4),
    .a(n4bitto7segment_7_a), .b(n4bitto7segment_7_b), .c(n4bitto7segment_7_c), .d(n4bitto7segment_7_d),
    .e(n4bitto7segment_7_e), .f(n4bitto7segment_7_f), .g(n4bitto7segment_7_g));
  clock clock_4 (
    .Set_Time(Set_Time_Manually), .Time_Input(clock_1_out_5), .Clock(clock_3_out), .Reset(Reset_Button_out),
    .out_5(clock_4_out_5));
  _6bittobcd u_6bittobcd_4 (
    .a(clock_4_out_5[5]), .b(clock_4_out_5[4]), .c(clock_4_out_5[3]), .d(clock_4_out_5[2]),
    .e(clock_4_out_5[1]), .f(clock_4_out_5[0]), .op1(n6bittobcd_4_op1), .op2(n6bittobcd_4_op2),
    .op3(n6bittobcd_4_op3), .op4(n6bittobcd_4_op4), .ha1(n6bittobcd_4_ha1), .ha2(n6bittobcd_4_ha2),
    .ha3(n6bittobcd_4_ha3), .ha4(n6bittobcd_4_ha4));
  _7_Segment_Display u_7_segment_display_8 (
    .g(n4bitto7segment_8_g), .f(n4bitto7segment_8_f), .a(n4bitto7segment_8_a), .b(n4bitto7segment_8_b),
    .e(n4bitto7segment_8_e), .d(n4bitto7segment_8_d), .c(n4bitto7segment_8_c));  // open: dp
  _4bitto7segment u_4bitto7segment_8 (
    .in_1(n6bittobcd_4_ha1), .in_2(n6bittobcd_4_ha2), .in_3(n6bittobcd_4_ha3), .in_4(n6bittobcd_4_ha4),
    .a(n4bitto7segment_8_a), .b(n4bitto7segment_8_b), .c(n4bitto7segment_8_c), .d(n4bitto7segment_8_d),
    .e(n4bitto7segment_8_e), .f(n4bitto7segment_8_f), .g(n4bitto7segment_8_g));
  _7_Segment_Display u_7_segment_display_9 (
    .g(n4bitto7segment_9_g), .f(n4bitto7segment_9_f), .a(n4bitto7segment_9_a), .b(n4bitto7segment_9_b),
    .e(n4bitto7segment_9_e), .d(n4bitto7segment_9_d), .c(n4bitto7segment_9_c));  // open: dp
  nor nor_1 (nor_1_out, clock_4_out_5[0], clock_4_out_5[1], clock_4_out_5[2], clock_4_out_5[3], clock_4_out_5[4], clock_4_out_5[5]);
  or or_1 (or_1_out, nor_1_out, Set_Time_Manually);
  _4bitto7segment u_4bitto7segment_9 (
    .in_1(n6bittobcd_5_op1), .in_2(n6bittobcd_5_op2), .in_3(n6bittobcd_5_op3), .in_4(n6bittobcd_5_op4),
    .a(n4bitto7segment_9_a), .b(n4bitto7segment_9_b), .c(n4bitto7segment_9_c), .d(n4bitto7segment_9_d),
    .e(n4bitto7segment_9_e), .f(n4bitto7segment_9_f), .g(n4bitto7segment_9_g));
  clock clock_5 (
    .Set_Time(Set_Time_Manually), .Time_Input(clock_2_out_5), .Clock(or_1_out), .Reset(Reset_Button_out),
    .out_5(clock_5_out_5));
  _6bittobcd u_6bittobcd_5 (
    .a(clock_5_out_5[5]), .b(clock_5_out_5[4]), .c(clock_5_out_5[3]), .d(clock_5_out_5[2]),
    .e(clock_5_out_5[1]), .f(clock_5_out_5[0]), .op1(n6bittobcd_5_op1), .op2(n6bittobcd_5_op2),
    .op3(n6bittobcd_5_op3), .op4(n6bittobcd_5_op4), .ha1(n6bittobcd_5_ha1), .ha2(n6bittobcd_5_ha2),
    .ha3(n6bittobcd_5_ha3), .ha4(n6bittobcd_5_ha4));
  _7_Segment_Display u_7_segment_display_10 (
    .g(n4bitto7segment_10_g), .f(n4bitto7segment_10_f), .a(n4bitto7segment_10_a), .b(n4bitto7segment_10_b),
    .e(n4bitto7segment_10_e), .d(n4bitto7segment_10_d), .c(n4bitto7segment_10_c));  // open: dp
  _4bitto7segment u_4bitto7segment_10 (
    .in_1(n6bittobcd_5_ha1), .in_2(n6bittobcd_5_ha2), .in_3(n6bittobcd_5_ha3), .in_4(n6bittobcd_5_ha4),
    .a(n4bitto7segment_10_a), .b(n4bitto7segment_10_b), .c(n4bitto7segment_10_c), .d(n4bitto7segment_10_d),
    .e(n4bitto7segment_10_e), .f(n4bitto7segment_10_f), .g(n4bitto7segment_10_g));
  _7_Segment_Display u_7_segment_display_11 (
    .g(n4bitto7segment_11_g), .f(n4bitto7segment_11_f), .a(n4bitto7segment_11_a), .b(n4bitto7segment_11_b),
    .e(n4bitto7segment_11_e), .d(n4bitto7segment_11_d), .c(n4bitto7segment_11_c));  // open: dp
  nor nor_2 (nor_2_out, clock_5_out_5[0], clock_5_out_5[1], clock_5_out_5[2], clock_5_out_5[3], clock_5_out_5[4], clock_5_out_5[5]);
  _4bitto7segment u_4bitto7segment_11 (
    .in_1(n6bittobcd_6_op1), .in_2(n6bittobcd_6_op2), .in_3(n6bittobcd_6_op3), .in_4(n6bittobcd_6_op4),
    .a(n4bitto7segment_11_a), .b(n4bitto7segment_11_b), .c(n4bitto7segment_11_c), .d(n4bitto7segment_11_d),
    .e(n4bitto7segment_11_e), .f(n4bitto7segment_11_f), .g(n4bitto7segment_11_g));
  or or_2 (or_2_out, nor_2_out, Set_Time_Manually);
  hourclock hourclock_2 (
    .Set_Time(Set_Time_Manually), .Time_Input(hourclock_1_out_5), .Clock(or_2_out), .Reset(Reset_Button_out),
    .out_5(hourclock_2_out_5));
  _6bittobcd u_6bittobcd_6 (
    .a(hourclock_2_out_5[5]), .b(hourclock_2_out_5[4]), .c(hourclock_2_out_5[3]), .d(hourclock_2_out_5[2]),
    .e(hourclock_2_out_5[1]), .f(hourclock_2_out_5[0]), .op1(n6bittobcd_6_op1), .op2(n6bittobcd_6_op2),
    .op3(n6bittobcd_6_op3), .op4(n6bittobcd_6_op4), .ha1(n6bittobcd_6_ha1), .ha2(n6bittobcd_6_ha2),
    .ha3(n6bittobcd_6_ha3), .ha4(n6bittobcd_6_ha4));
  _7_Segment_Display u_7_segment_display_12 (
    .g(n4bitto7segment_12_g), .f(n4bitto7segment_12_f), .a(n4bitto7segment_12_a), .b(n4bitto7segment_12_b),
    .e(n4bitto7segment_12_e), .d(n4bitto7segment_12_d), .c(n4bitto7segment_12_c));  // open: dp
  _4bitto7segment u_4bitto7segment_12 (
    .in_1(n6bittobcd_6_ha1), .in_2(n6bittobcd_6_ha2), .in_3(n6bittobcd_6_ha3), .in_4(n6bittobcd_6_ha4),
    .a(n4bitto7segment_12_a), .b(n4bitto7segment_12_b), .c(n4bitto7segment_12_c), .d(n4bitto7segment_12_d),
    .e(n4bitto7segment_12_e), .f(n4bitto7segment_12_f), .g(n4bitto7segment_12_g));

  // Notes on the sheet:
  //   SECONDS
  //   Time Setter
  //   MINUTES
  //   HOURS
  //   SECONDS
  //   MINUTES
  //   Clock
  //   HOURS
endmodule

module clock (
  input  Set_Time,
  input  [5:0] Time_Input,
  input  Clock,
  input  Reset,
  output [5:0] out_5
);

  wire and_1_out, not_1_out, or_1_out, xnor_1_out, xnor_2_out, xnor_3_out, xnor_4_out, xnor_5_out, xnor_6_out;

  Counter #(.width(6), .max('h3f)) counter_1 (
    .load(Set_Time), .D(Time_Input), .count(not_1_out), .Q(out_5), .clk(Clock), .clr(or_1_out));  // open: carry
  not not_1 (not_1_out, Set_Time);
  or or_1 (or_1_out, Reset, and_1_out);
  xnor xnor_1 (xnor_1_out, out_5[0], 1'b0);
  xnor xnor_2 (xnor_2_out, out_5[1], 1'b0);
  xnor xnor_3 (xnor_3_out, out_5[2], 1'b1);
  xnor xnor_4 (xnor_4_out, out_5[3], 1'b1);
  xnor xnor_5 (xnor_5_out, out_5[4], 1'b1);
  xnor xnor_6 (xnor_6_out, out_5[5], 1'b1);
  and and_1 (and_1_out, xnor_1_out, xnor_2_out, xnor_3_out, xnor_4_out, xnor_5_out, xnor_6_out);
endmodule

module _6bittobcd (
  input  a,
  input  b,
  input  c,
  input  d,
  input  e,
  input  f,
  output op1,
  output op2,
  output op3,
  output op4,
  output ha1,
  output ha2,
  output ha3,
  output ha4
);

  wire nand_1_out, nand_2_out, nand_3_out, nand_4_out, nand_5_out, nand_6_out, nand_7_out, nand_8_out,
       nand_9_out, nand_10_out, nand_11_out, nand_12_out, nand_13_out, nand_14_out, nand_15_out, nand_16_out,
       nand_17_out, nand_18_out, nand_19_out, nand_20_out, nand_21_out, nand_22_out, nand_23_out,
       nand_24_out, nand_25_out, nand_26_out, nand_27_out, nand_28_out, nand_29_out, nand_30_out,
       nand_31_out, nand_32_out, nand_33_out, nand_34_out, nand_35_out, nand_36_out, nand_37_out,
       nand_38_out, nand_39_out, nand_40_out, nand_41_out, nand_42_out, nand_43_out, nand_44_out,
       nand_45_out, nand_46_out, nand_47_out, nand_48_out, nand_49_out, nand_50_out, nand_51_out,
       nand_52_out, nand_53_out, nand_54_out, nand_55_out, nand_56_out, nand_57_out, nand_58_out,
       nand_59_out, nand_60_out, nand_61_out, nand_62_out, nand_63_out, nand_64_out, nand_65_out,
       nand_66_out, nand_67_out, nand_68_out, nand_69_out, nand_70_out, nand_71_out, nand_72_out,
       nand_73_out, nand_74_out, nand_75_out, nand_76_out, nand_77_out, nand_78_out, nand_79_out,
       nand_80_out, nand_81_out, nand_82_out, nand_83_out, nand_85_out, nand_86_out, nand_87_out,
       nand_88_out, nand_89_out, nand_90_out, nand_91_out, nand_92_out, nand_93_out, nand_94_out,
       nand_95_out, nand_96_out, nand_97_out, nand_98_out, nand_99_out, nand_100_out, nand_101_out,
       nand_102_out, nand_103_out, nand_104_out, nand_105_out, nand_106_out, nand_107_out, nand_108_out,
       nand_109_out, nand_110_out, nand_111_out, nand_112_out, nand_113_out, nand_114_out, nand_116_out,
       nand_117_out, nand_118_out, nand_119_out, nand_120_out, nand_121_out, nand_122_out, nand_123_out,
       nand_124_out, nand_125_out, nand_126_out, nand_127_out, nand_128_out, nand_129_out, nand_130_out,
       nand_131_out, nand_132_out;

  nand nand_1 (nand_1_out, a, c);
  nand nand_2 (nand_2_out, a, b);
  nand nand_3 (nand_3_out, a, a);
  nand nand_4 (nand_4_out, a, a);
  nand nand_5 (nand_5_out, b, b);
  nand nand_6 (nand_6_out, c, c);
  nand nand_7 (nand_7_out, a, a);
  nand nand_8 (nand_8_out, b, b);
  nand nand_9 (nand_9_out, a, a);
  nand nand_10 (nand_10_out, b, b);
  nand nand_11 (nand_11_out, a, a);
  nand nand_12 (nand_12_out, a, a);
  nand nand_13 (nand_13_out, c, c);
  nand nand_14 (nand_14_out, d, d);
  nand nand_15 (nand_15_out, b, b);
  nand nand_16 (nand_16_out, c, c);
  nand nand_17 (nand_17_out, c, c);
  nand nand_18 (nand_18_out, c, c);
  nand nand_19 (nand_19_out, d, d);
  nand nand_20 (nand_20_out, a, a);
  nand nand_21 (nand_21_out, b, b);
  nand nand_22 (nand_22_out, d, d);
  nand nand_23 (nand_23_out, e, e);
  nand nand_24 (nand_24_out, a, a);
  nand nand_25 (nand_25_out, c, c);
  nand nand_26 (nand_26_out, d, d);
  nand nand_27 (nand_27_out, a, a);
  nand nand_28 (nand_28_out, e, e);
  nand nand_29 (nand_29_out, b, b);
  nand nand_30 (nand_30_out, c, c);
  nand nand_31 (nand_31_out, c, c);
  nand nand_32 (nand_32_out, d, d);
  nand nand_33 (nand_33_out, e, e);
  nand nand_34 (nand_34_out, a, a);
  nand nand_35 (nand_35_out, b, b);
  nand nand_36 (nand_36_out, c, c);
  nand nand_37 (nand_37_out, a, a);
  nand nand_38 (nand_38_out, b, b);
  nand nand_39 (nand_39_out, a, a);
  nand nand_40 (nand_40_out, d, d);
  nand nand_41 (nand_41_out, e, e);
  nand nand_42 (nand_42_out, a, a);
  nand nand_43 (nand_43_out, d, d);
  nand nand_44 (nand_44_out, d, d);
  nand nand_45 (nand_45_out, e, e);
  nand nand_46 (nand_46_out, b, b);
  nand nand_47 (nand_47_out, c, c);
  nand nand_48 (nand_48_out, d, d);
  nand nand_49 (nand_49_out, b, b);
  nand nand_50 (nand_50_out, e, e);
  nand nand_51 (nand_51_out, b, b);
  nand nand_52 (nand_52_out, a, a);
  nand nand_53 (nand_53_out, b, b);
  nand nand_54 (nand_54_out, c, c);
  nand nand_55 (nand_55_out, a, a);
  nand nand_56 (nand_56_out, c, c);
  nand nand_57 (nand_57_out, a, a);
  nand nand_58 (nand_58_out, b, b);
  nand nand_59 (nand_59_out, e, e);
  nand nand_60 (nand_60_out, a, a);
  nand nand_61 (nand_61_out, b, b);
  nand nand_62 (nand_62_out, f, f);
  nand nand_63 (nand_63_out, a, a);
  nand nand_64 (nand_64_out, c, c);
  nand nand_65 (nand_65_out, d, d);
  nand nand_66 (nand_66_out, e, e);
  nand nand_67 (nand_67_out, a, a);
  nand nand_68 (nand_68_out, d, d);
  nand nand_69 (nand_69_out, b, b);
  nand nand_70 (nand_70_out, c, c);
  nand nand_71 (nand_71_out, e, e);
  nand nand_72 (nand_72_out, c, c);
  nand nand_73 (nand_73_out, e, e);
  nand nand_74 (nand_74_out, b, b);
  nand nand_75 (nand_75_out, d, d);
  nand nand_76 (nand_76_out, e, e);
  nand nand_77 (nand_77_out, a, a);
  nand nand_78 (nand_78_out, b, b);
  nand nand_79 (nand_79_out, f, f);
  nand nand_80 (nand_80_out, a, a);
  nand nand_81 (nand_81_out, c, c);
  nand nand_82 (nand_82_out, d, d);
  nand nand_83 (nand_83_out, e, e);
  nand nand_84 (op2, nand_1_out, nand_2_out);
  nand nand_85 (nand_85_out, nand_3_out, b, d);
  nand nand_86 (nand_86_out, nand_4_out, b, c);
  nand nand_87 (nand_87_out, b, c, d);
  nand nand_88 (nand_88_out, a, nand_5_out, nand_6_out);
  nand nand_89 (nand_89_out, nand_7_out, nand_8_out, c, e);
  nand nand_90 (nand_90_out, nand_9_out, nand_10_out, c, d);
  nand nand_91 (nand_91_out, nand_11_out, c, d, e);
  nand nand_92 (nand_92_out, nand_12_out, b, nand_13_out, nand_14_out);
  nand nand_93 (nand_93_out, a, nand_15_out, nand_16_out);
  nand nand_94 (nand_94_out, a, nand_17_out, e);
  nand nand_95 (nand_95_out, a, nand_18_out, d);
  nand nand_96 (nand_96_out, a, b, c, nand_19_out);
  nand nand_97 (nand_97_out, nand_20_out, nand_21_out, c, nand_22_out, nand_23_out);
  nand nand_98 (nand_98_out, nand_24_out, b, nand_25_out, nand_26_out, e);
  nand nand_99 (nand_99_out, nand_27_out, b, c, d, nand_28_out);
  nand nand_100 (nand_100_out, a, nand_29_out, nand_30_out, d, e);
  nand nand_101 (nand_101_out, a, b, nand_31_out, nand_32_out, nand_33_out);
  nand nand_102 (nand_102_out, a, b, c, e);
  nand nand_103 (nand_103_out, nand_34_out, nand_35_out, nand_36_out, d);
  nand nand_104 (nand_104_out, nand_37_out, nand_38_out, d, e, f);
  nand nand_105 (nand_105_out, nand_39_out, b, nand_40_out, nand_41_out);
  nand nand_106 (nand_106_out, nand_42_out, b, c, nand_43_out);
  nand nand_107 (nand_107_out, b, c, nand_44_out, nand_45_out);
  nand nand_108 (nand_108_out, a, nand_46_out, nand_47_out, nand_48_out, e);
  nand nand_109 (nand_109_out, a, nand_49_out, d, nand_50_out);
  nand nand_110 (nand_110_out, a, nand_51_out, c, d);
  nand nand_111 (nand_111_out, a, b, d, e);
  nand nand_112 (nand_112_out, c, c);
  nand nand_113 (nand_113_out, d, d);
  nand nand_114 (nand_114_out, e, e);
  nand nand_115 (op3, nand_85_out, nand_86_out, nand_87_out, nand_88_out);
  nand nand_116 (nand_116_out, nand_52_out, nand_53_out, nand_54_out, e);
  nand nand_117 (nand_117_out, nand_55_out, nand_56_out, d, e);
  nand nand_118 (nand_118_out, nand_57_out, nand_58_out, c, d, nand_59_out);
  nand nand_119 (nand_119_out, nand_60_out, nand_61_out, c, d, nand_62_out);
  nand nand_120 (nand_120_out, nand_63_out, b, nand_64_out, nand_65_out, nand_66_out, f);
  nand nand_121 (nand_121_out, nand_67_out, b, c, nand_68_out, e);
  nand nand_122 (nand_122_out, a, nand_69_out, nand_70_out, nand_71_out);
  nand nand_123 (nand_123_out, a, nand_72_out, d, nand_73_out);
  nand nand_124 (nand_124_out, a, nand_74_out, c, e);
  nand nand_125 (nand_125_out, a, b, c, nand_75_out, nand_76_out);
  nand nand_126 (nand_126_out, nand_112_out, f);
  nand nand_127 (nand_127_out, nand_113_out, f);
  nand nand_128 (nand_128_out, nand_114_out, f);
  nand nand_129 (nand_129_out, nand_77_out, nand_78_out, c, d, e, nand_79_out);
  nand nand_130 (nand_130_out, nand_80_out, b, nand_81_out, nand_82_out, nand_83_out);
  nand nand_131 (nand_131_out, b, f);
  nand nand_132 (nand_132_out, a, f);
  nand nand_133 (op4, nand_89_out, nand_90_out, nand_91_out, nand_92_out, nand_93_out, nand_94_out, nand_95_out, nand_96_out);
  nand nand_134 (ha1, nand_97_out, nand_98_out, nand_99_out, nand_100_out, nand_101_out, nand_102_out);
  nand nand_135 (ha2, nand_103_out, nand_104_out, nand_105_out, nand_106_out, nand_107_out, nand_108_out, nand_109_out, nand_110_out, nand_111_out);
  nand nand_136 (ha3, nand_116_out, nand_117_out, nand_118_out, nand_119_out, nand_120_out, nand_121_out, nand_122_out, nand_123_out, nand_124_out, nand_125_out);
  nand nand_137 (ha4, nand_126_out, nand_127_out, nand_128_out, nand_129_out, nand_130_out, nand_131_out, nand_132_out);

  assign op1 = 1'b0;
endmodule

module _4bitto7segment (
  input  in_1,
  input  in_2,
  input  in_3,
  input  in_4,
  output a,
  output b,
  output c,
  output d,
  output e,
  output f,
  output g
);

  wire and_1_out, and_2_out, and_3_out, and_4_out, and_5_out, and_6_out, and_7_out, and_8_out, and_9_out,
       and_10_out, and_11_out, and_12_out, and_13_out, and_14_out, and_15_out, and_16_out, not_1_out,
       not_2_out, not_3_out, not_4_out, not_5_out, not_6_out, not_7_out, not_8_out, not_9_out, not_10_out,
       not_11_out, not_12_out, not_13_out, not_14_out, not_15_out, not_16_out, not_17_out, not_18_out,
       not_19_out, not_20_out, not_21_out;

  not not_1 (not_1_out, in_2);
  and and_1 (and_1_out, not_1_out, not_2_out);
  not not_2 (not_2_out, in_4);
  and and_2 (and_2_out, in_2, in_4);
  not not_3 (not_3_out, in_2);
  not not_4 (not_4_out, in_3);
  and and_3 (and_3_out, not_4_out, not_5_out);
  not not_5 (not_5_out, in_4);
  and and_4 (and_4_out, in_3, in_4);
  not not_6 (not_6_out, in_3);
  or or_1 (c, not_6_out, in_4, in_2);
  not not_7 (not_7_out, in_2);
  and and_5 (and_5_out, not_7_out, not_8_out);
  not not_8 (not_8_out, in_4);
  not not_9 (not_9_out, in_2);
  and and_6 (and_6_out, not_9_out, in_3);
  and and_7 (and_7_out, in_3, not_10_out);
  not not_10 (not_10_out, in_4);
  not not_11 (not_11_out, in_3);
  and and_8 (and_8_out, in_2, not_11_out, in_4);
  not not_12 (not_12_out, in_2);
  and and_9 (and_9_out, not_12_out, not_13_out);
  not not_13 (not_13_out, in_4);
  and and_10 (and_10_out, in_3, not_14_out);
  not not_14 (not_14_out, in_4);
  not not_15 (not_15_out, in_3);
  and and_11 (and_11_out, not_15_out, not_16_out);
  not not_16 (not_16_out, in_4);
  and and_12 (and_12_out, in_2, not_17_out);
  not not_17 (not_17_out, in_3);
  and and_13 (and_13_out, in_2, not_18_out);
  not not_18 (not_18_out, in_4);
  not not_19 (not_19_out, in_2);
  and and_14 (and_14_out, not_19_out, in_3);
  and and_15 (and_15_out, in_2, not_20_out);
  not not_20 (not_20_out, in_3);
  and and_16 (and_16_out, in_2, not_21_out);
  not not_21 (not_21_out, in_4);
  or or_2 (a, and_1_out, in_3, and_2_out, in_1);
  or or_3 (b, not_3_out, and_3_out, and_4_out);
  or or_4 (d, and_5_out, and_6_out, and_7_out, and_8_out, in_1);
  or or_5 (e, and_9_out, and_10_out);
  or or_6 (f, and_11_out, and_12_out, and_13_out, in_1);
  or or_7 (g, and_14_out, and_15_out, and_16_out, in_1);
endmodule

module hourclock (
  input  Set_Time,
  input  [5:0] Time_Input,
  input  Clock,
  input  Reset,
  output [5:0] out_5
);

  wire and_1_out, not_1_out, or_1_out, xnor_1_out, xnor_2_out, xnor_3_out, xnor_4_out, xnor_5_out, xnor_6_out;

  Counter #(.width(6), .max('h3f)) counter_1 (
    .load(Set_Time), .D(Time_Input), .count(not_1_out), .Q(out_5), .clk(Clock), .clr(or_1_out));  // open: carry
  not not_1 (not_1_out, Set_Time);
  or or_1 (or_1_out, Reset, and_1_out);
  xnor xnor_1 (xnor_1_out, out_5[0], 1'b0);
  xnor xnor_2 (xnor_2_out, out_5[1], 1'b0);
  xnor xnor_3 (xnor_3_out, out_5[2], 1'b0);
  xnor xnor_4 (xnor_4_out, out_5[3], 1'b1);
  xnor xnor_5 (xnor_5_out, out_5[4], 1'b1);
  xnor xnor_6 (xnor_6_out, out_5[5], 1'b0);
  and and_1 (and_1_out, xnor_1_out, xnor_2_out, xnor_3_out, xnor_4_out, xnor_5_out, xnor_6_out);
endmodule
